# Fritzing sketch FinalProject (saved by Fritzing 1.0.4)
breadboards: 1

parts:
  J1 = STM32 Nucleo boards
  Part1 = BH1750
  U1 = LCD-16X2 [package=lcd-8x2]
  LED1 = smd LED [color="Green (555nm)" package="0805 [SMD]"]
  LED2 = smd LED [color="Green (555nm)" package="0805 [SMD]"]
  LED3 = smd LED [color="Yellow (574nm)" package="0805 [SMD]"]
  LED4 = smd LED [color="Yellow (574nm)" package="0805 [SMD]"]
  LED5 = smd LED [color="Red (633nm)" package="0805 [SMD]"]
  LED6 = smd LED [color="Red (633nm)" package="0805 [SMD]"]
  V1 = DC Power [voltage=5V internal_resistance=0.1Ω]
  R1 = Resistor [tolerance=±5% resistance=470 package="0805 [SMD]"]
  R2 = Resistor [tolerance=±5% resistance=470 package="0805 [SMD]"]
  R3 = Resistor [tolerance=±5% resistance=470 package="0805 [SMD]"]
  R4 = Resistor [tolerance=±5% resistance=470 package="0805 [SMD]"]
  R5 = Resistor [tolerance=±5% resistance=470 package="0805 [SMD]"]
  R6 = Resistor [tolerance=±5% resistance=470 package="0805 [SMD]"]
  R7 = TRIMPOT [maximum_resistance=10kΩ knob_status=50% power=0.5W package=3362u-2]

nets:
  N1: J1.PA11, U1.DB7
  N2: J1.5V#338, U1.VDD, U1.A, R7.CCW
  GND: J1.GND#880, Part1.GND, V1.V-, R1.Pin_1, R2.Pin_1, R3.Pin_1, R4.Pin_1, R5.Pin_1, R6.Pin_1
  N3: J1.GND#1157, Part1.ADDR, U1.VSS, U1.R_W, U1.K, R7.CW
  3V3: J1.3V3, Part1.VCC
  N4: J1.5V#1187, V1.V+
  N5: J1.PB2, LED3.anode
  N6: J1.PB1, LED2.anode
  N7: J1.PB8, Part1.SCL
  N8: J1.PB9, Part1.SDA
  N9: J1.PA6, U1.RS
  N10: J1.PA7, U1.E
  N11: J1.PA9, U1.DB5
  N12: J1.PA8, U1.DB4
  N13: J1.PB4, LED5.anode
  N14: J1.PB5, LED6.anode
  N15: J1.PB3, LED4.anode
  N16: J1.PA10, U1.DB6
  N17: J1.PB0, LED1.anode
  N18: U1.VO, R7.WIPER
  N19: LED1.cathode, R1.Pin_0
  N20: LED2.cathode, R2.Pin_0
  N21: LED3.cathode, R3.Pin_0
  N22: LED4.cathode, R4.Pin_0
  N23: LED5.cathode, R5.Pin_0
  N24: LED6.cathode, R6.Pin_0

custom parts:
  BH1750: Light Sensor
