# Fritzing sketch ADXL SPI - Schematic (saved by Fritzing 1.0.4)
breadboards: 1

parts:
  J1 = STM32 Nucleo boards
  V1 = DC Power [voltage=5V internal_resistance=0.1Ω]
  Part2 = Triple Axis Accelerometer Breakout - ADXL345

nets:
  3V3: J1.3v3, Part2.VCC
  N1: J1.GND#339, Part2.GND
  GND: J1.GND#881, V1.V-
  N2: J1.D11_PWM/MOSI, Part2.SDA
  N3: J1.D12/MISO, Part2.SDO
  N4: J1.A5/SCL, Part2.SCL
  N5: J1.5V, V1.V+
  N6: J1.PB6, Part2.CS
