# Fritzing sketch TMP 102 - I2C Schematic (saved by Fritzing 1.0.4)
breadboards: 1

parts:
  J1 = STM32 Nucleo boards
  V1 = DC Power [voltage=5V internal_resistance=0.1Ω]
  U1 = TMP102 [package=sot563]
  Pullup_1 = Resistor [tolerance=±5% power=0.25W resistance=2.2k package=THT]
  Pullup_2 = Resistor [tolerance=±5% power=0.25W resistance=2.2k package=THT]

nets:
  3V3: J1.3v3, U1.VCC, Pullup_1.Pin_1, Pullup_2.Pin_1
  N1: J1.5V, V1.V+
  GND: J1.GND, V1.V-, U1.GND
  N2: J1.PB8, U1.SCL, Pullup_2.Pin_0
  N3: J1.PB9, U1.SDA, Pullup_1.Pin_0
