# Fritzing sketch Lab 3 Schematic (saved by Fritzing 1.0.4)
breadboards: 1

parts:
  Thermistor_Cirucuit = Arduino Mega ADK (Rev3)
  V1 = DC Power [voltage=5V]
  R1 = Resistor [tolerance=±5% resistance=10k package="2512 [SMD]"]
  R2 = Temperature Sensor (Thermistor) [thermistor_type=NTC package=THT]

nets:
  N1: Thermistor_Cirucuit.A0, R1.Pin_1, R2.pin_1
  GND: Thermistor_Cirucuit.GND, V1.V-, R2.pin_0
  N2: Thermistor_Cirucuit.IOREF, Thermistor_Cirucuit.5V, R1.Pin_0
  N3: Thermistor_Cirucuit.VIN, V1.V+
