# Fritzing sketch Alt Blink Wiring Diagram (saved by Fritzing 1.0.4)
breadboards: 1

parts:
  J1 = STM32 Nucleo boards
  V1 = DC Power [voltage=3.3V internal_resistance=0.1Ω]
  LED1 = LED - 3mm [color="Red (633nm)" current=0.030A package="3 mm [THT]"]
  LED2 = LED - 3mm [color="Blue (525nm)" current=0.030A package="3 mm [THT]"]
  R1 = 470 Ω Resistor [package="1206 [SMD]"]
  R2 = 470 Ω Resistor [package="1206 [SMD]"]

nets:
  GND: J1.GND, V1.V-, LED1.cathode, LED2.cathode
  N1: J1.VIN, V1.V+
  N2: J1.PA6, R1.Pin_1
  N3: J1.PA7, R2.Pin_1
  N4: LED1.anode, R1.Pin_0
  N5: LED2.anode, R2.Pin_0

custom parts:
  470 Ω Resistor: A generic resistor
