# Fritzing sketch LCD Wiring Diagram (saved by Fritzing 1.0.4)
breadboards: 1

parts:
  J1 = STM32 Nucleo boards
  V1 = DC Power [voltage=5V]
  U1 = POT [knob_status=50% power=0.5W package=alps_pot]
  U2 = LCD-16X2 [package=lcd-8x2-kit]

nets:
  N1: J1.PA11, U2.DB7
  GND: J1.GND, V1.V-, U1.E, U2.VSS, U2.K
  5V: J1.5V, U1.A, U2.VDD, U2.A
  N2: J1.VIN, V1.V+
  N3: J1.PA6, U2.RS
  N4: J1.PA7, U2.E
  N5: J1.PA9, U2.DB5
  N6: J1.PA8, U2.DB4
  N7: J1.PA10, U2.DB6
  N8: U1.S, U2.VO
