# Fritzing sketch Schematic (saved by Fritzing 1.0.4)
breadboards: 1

parts:
  J2 = STM32 Nucleo boards
  V2 = DC Power [voltage=5V]
  T1 = LM35 Temperature Sensor [package="TO92 [THT]"]
  LED1 = smd LED [color="Blue (525nm)" package="0805 [SMD]"]
  R1 = Resistor [tolerance=±5% resistance=330 package="0402 [SMD]"]

nets:
  N1: J2.5V, T1.+Vs
  GND: J2.GND#880, V2.V-
  N2: J2.GND#1188, T1.GND, LED1.cathode
  N3: J2.VIN, V2.V+
  N4: J2.PC1, R1.Pin_0
  N5: J2.PC2, T1.Vout
  N6: LED1.anode, R1.Pin_1
